// Logisim project Previo3.circ as structural Verilog: 1 circuit, main circuit main
module main (
  input  X,
  input  Y,
  input  Z,
  output Salida
);

  wire and_1_out, and_2_out, and_3_out, and_4_out, not_1_out, not_2_out;

  not not_1 (not_1_out, X);
  not not_2 (not_2_out, Y);
  and and_1 (and_1_out, not_1_out, Z);
  and and_2 (and_2_out, not_1_out, Y);
  and and_3 (and_3_out, Y, Z);
  and and_4 (and_4_out, X, not_2_out, Z);
  or or_1 (Salida, and_1_out, and_2_out, and_3_out, and_4_out);
endmodule
